# Fritzing sketch Fritzing Diagram (saved by Fritzing 0.9.3b)
breadboards: 1

parts:
  Part1 = SparkFun ESP8266 Thing
  S1 = Momentary Switch [package=tactile_switch_smd]
  LED1 = RGB LED (com. anode, rbg) [package="5 mm [THT]"]
  IC2 = iAQ-C [chip_label=IC package="DIP (Dual Inline) [THT]"]

nets:
  N1: Part1.GND, S1.1, IC2.pin3
  N2: Part1.VCC, LED1.common_anode, IC2.pin6
  N3: Part1.GPIO2, IC2.pin4
  N4: Part1.GPIO14, IC2.pin2
  N5: Part1.GPIO5, S1.4
  N6: Part1.GPIO4, LED1.red_cathode
  N7: Part1.GPIO13, LED1.blue_cathode
  N8: Part1.GPIO12, LED1.green_cathode

custom parts:
  iAQ-C: A DIP stand-in part for whatever IC you want. With 8 pins on a 300mil dual inline package (DIP) footprint.
